# Fritzing sketch Sketch (saved by Fritzing 0.9.3b)
breadboards: 1

parts:
  Part1 = Arduino Uno (Rev3)
  Ânodo_(+)_‌‌_‌‌_‌‌_‌‌_‌‌_‌‌_‌‌‌‌_‌‌_‌‌_‌‌_‌‌‌‌_‌‌_‌‌_‌‌_‌‌‌‌_‌‌_‌‌_‌‌_‌‌_‌‌‌‌‌‌_‌‌Cátodo_(-) = Resonator [package=THT]  # not connected
  part = Resistor [tolerance=±5% resistance=470 package=THT]  # not connected
  part_2 = Electrolytic Capacitor [capacitance=220µF package="100 mil [THT, electrolytic]"]

nets:
  N1: Part1.A0, part_2.-
  N2: Part1.GND, part_2.+

custom parts:
  Resonator: Ceramic resonator with built-in capacitors
